# Fritzing sketch fortuna (saved by Fritzing 0.9.3b)
breadboards: 1

parts:
  Arduino_UNO = Arduino Uno (Rev3)
  9-Volt_Battery = Battery block 9V
  IC1 = Dual Op-Amp [package=dip08]
  IC2 = Dual Op-Amp [package=dip08]
  R1 = Resistor [tolerance=±5% resistance=2.7k package=THT]
  R2 = Resistor [tolerance=±5% resistance=2.7k package=THT]
  R3 = Resistor [tolerance=±5% resistance=2.7k package=THT]
  R4 = Resistor [tolerance=±5% resistance=2.7k package=THT]
  R5 = Resistor [tolerance=±5% resistance=2.7k package=THT]
  R6 = Resistor [tolerance=±5% resistance=2.7k package=THT]
  Left_Photocell = PHOTOCELL [package=photocell]
  Right_Photocell = PHOTOCELL [package=photocell]
  Piezo_Buzzer = Piezo Speaker
  Right_Motor = DC Motor
  Left_Motor = DC Motor
  Right_Diode = Rectifier Diode [part_number=1N4001 package="Melf DO-213 AB [SMD]"]
  Left_Diode = Rectifier Diode [part_number=1N4001 package="Melf DO-213 AB [SMD]"]
  Left_Transistor = TRANSISTOR_NPN [package=to-92-ammo]
  R7 = Resistor [tolerance=±5% resistance=1k package=THT]
  R8 = Resistor [tolerance=±5% resistance=1k package=THT]
  Right_Transistor = TRANSISTOR_NPN [package=to-92-ammo]
  R9 = Resistor [tolerance=±5% resistance=10k package=THT]
  Microphone = Microphone
  C1 = Ceramic Capacitor [capacitance=1µF package="100 mil [THT, multilayer]"]
  R10 = Resistor [tolerance=±5% resistance=2.7k package=THT]
  R11 = Resistor [tolerance=±5% resistance=100k package=THT]
  R12 = Resistor [tolerance=±5% resistance=10k package=THT]
  R13 = Resistor [tolerance=±5% resistance=10k package=THT]

nets:
  N1: Arduino_UNO.A0, IC1.B_OUT
  N2: Arduino_UNO.A3, IC1.A_OUT, R11.Pin_1
  N3: Arduino_UNO.A5/SCL, IC2.B_OUT
  N4: Arduino_UNO.D10_PWM/SS, R8.Pin_1
  N5: Arduino_UNO.D2, IC2.A_+IN
  N6: Arduino_UNO.D5_PWM, R7.Pin_1
  N7: Arduino_UNO.5V, IC1.A_V+, IC2.A_V+, R1.Pin_1, R4.Pin_1, Left_Photocell.P$2, Right_Photocell.P$1, R12.Pin_1
  N8: 9-Volt_Battery.-, IC1.A_V-, IC2.A_V-, R2.Pin_0, R3.Pin_1, R5.Pin_0, R6.Pin_1, Piezo_Buzzer.pin1, Left_Transistor.E, Right_Transistor.E, Microphone.pin1, R13.Pin_1
  N9: 9-Volt_Battery.+, Right_Motor.pin_1, Left_Motor.pin_2, Right_Diode.cathode, Left_Diode.cathode, R9.Pin_0
  N10: IC1.A_-IN, R10.Pin_0, R11.Pin_0
  N11: IC1.A_+IN, R12.Pin_0, R13.Pin_0
  N12: IC1.B_+IN, R3.Pin_0, Left_Photocell.P$1
  N13: IC1.B_-IN, R1.Pin_0, R2.Pin_1
  N14: IC2.A_OUT, IC2.A_-IN, Piezo_Buzzer.pin2
  N15: IC2.B_+IN, R6.Pin_0, Right_Photocell.P$2
  N16: IC2.B_-IN, R4.Pin_0, R5.Pin_1
  N17: Right_Motor.pin_2, Right_Diode.anode, Right_Transistor.C
  N18: Left_Motor.pin_1, Left_Diode.anode, Left_Transistor.C
  N19: Left_Transistor.B, R7.Pin_0
  N20: R8.Pin_0, Right_Transistor.B
  N21: R9.Pin_1, Microphone.pin2, C1.1
  N22: C1.0, R10.Pin_1

// code stored in the sketch: fortuna.ino
//****************************************************************************
//
// Project Name: Robot Collection - Project 01: Fortuna
//
// File Name: fortuna.ino
//
// Description: The robot...
//     moves forward by two motors on its left and right wings (wings)
//     automatically beeps when activating (mouth)
//     flashes the LEDs like an airplane at night
//     determines the ON-OFF status of the motors by two photocells (eyes)
//     listens to loud noise and changes behaviors of mouth and wings (ear)
//
// Compatibility: Arduino UNO
//
// Version:
//     1.0 (July 17, 2016)
//
// Phi Luu
// Portland, Oregon, United States
// Created March 13, 2016
// Updated August 13, 2016
//
//****************************************************************************

//**********Required Hardware I/O Connections**********
const int BUZZER = 2;       // Buzzer connected to 2
const int LMOTOR = 5;       // Left motor connected to ~5
const int RMOTOR = 10;      // Right motor connected to ~10
const int LPHOTO = A0;      // Left photocell connected to A0
const int RPHOTO = A5;      // Right photocell connected to A5
const int MICINP = A3;      // Microphone connected to A3
const int LLED = 4;         // Left LED connected to 4
const int RLED = 7;         // Right LED connected to 7

// set motors to use 50% PWM (possible values 0-255)
const int MPOW = 128;
// set microphone trigger threshold (possible values 0-1023)
const int MICTHRESH = 600;

//**********setup**********
// Put setup code here, to run once
// Inputs: None
// Outputs: None
void setup() {
    pinMode(LMOTOR, OUTPUT);  // set LMOTOR as OUTPUT
    pinMode(RMOTOR, OUTPUT);  // set RMOTOR as OUTPUT
    pinMode(BUZZER, OUTPUT);  // set BUZZER as OUTPUT
    pinMode(LLED, OUTPUT);    // set LLED as OUTPUT
    pinMode(RLED, OUTPUT);    // set RLED as OUTPUT
}

//**********beep**********
// Generates a square wave at a given frequency for ms miliseconds
// Inputs: pin    the pin number needed to make sound
//         freq   the frequency of the sound
//         ms     the duration
// Outputs: None
void beep(int pin, int freq, long ms) {
    long semiPer = (long) (1000000/(freq*2));
    long loops = (long) ((ms*1000)/(semiPer*2));
    for (int k = 0; k < loops; k++) {
        digitalWrite(pin, HIGH);        // set buzzer pin high
        delayMicroseconds(semiPer);     // for half of the period
        digitalWrite(pin, LOW);         // set buzzer pin low
        delayMicroseconds(semiPer);     // for the other half of the period
    }
}

//**********loop**********
// Put main code here, to run repeatedly
// Inputs: None
// Outputs: None
void loop() {
    // turn off both motors
    analogWrite(LMOTOR,0);
    analogWrite(RMOTOR,0);

    // beep a bunch of times
    for (int i = 1; i < 5; i++) {
        beep(BUZZER, 1000, 100*i);
        delay(100*i);
    }

    // listen to the microphone for ~100 ms
    int val;
    int maxVal = 0;
    for (int i = 1; i < 100; i++) {
        val = analogRead(MICINP);
        if (val > maxVal) {
            maxVal = val;
        }
        delay(1);
    }

    // if the largest voltage detected is above 1.77 V (3.3*550/1024),
    // commence the "beep dance" response
    if (maxVal > MICTHRESH) {
        // make the "siren" noise by alternating 1200 Hz and 800 Hz tones
        for (int i = 0; i < 5; i++) {
            beep(BUZZER, 1200, 100);
            beep(BUZZER, 800,  100);
        }
        // shake motors back and forth rapidly
        for (int i = 0; i < 3; i++) {
            analogWrite(RMOTOR, MPOW);
            delay(200);
            analogWrite(RMOTOR, 0);
            analogWrite(LMOTOR, MPOW);
            delay(200);
            analogWrite(LMOTOR, 0);
        }
        // make a series of tones with increasing frequency from 300-100 Hz
        for (int i = 30; i < 100; i += 1) {
            beep(BUZZER, 10*i, 10);
        }
        // then come back down
        for (int i = 100; i > 30; i -= 1) {
            beep(BUZZER, 10*i, 10);
        }
    }

    // flash the light like an airplane
    digitalWrite(LLED, HIGH);
    delay(10);
    digitalWrite(LLED, LOW);
    digitalWrite(RLED, HIGH);
    delay(10);
    digitalWrite(RLED, LOW);

    // read the status of photocells and adjust motor output
    // delay briefly to allow comparator outputs to settle
    delayMicroseconds(20);

    // check each photocell/circuit output and determine
    if (digitalRead(LPHOTO)) {
        analogWrite(LMOTOR, MPOW);  // whether to run on the left motor...
    }
    if (digitalRead(RPHOTO)) {      // ...or right motor
        analogWrite(RMOTOR, MPOW);
    }
    delay(500);                     // wait 500ms
}
